// Logisim project AC2 relatorio 3.circ as structural Verilog: 4 circuits, main circuit main
module main (
  input  in_1,
  input  in_2,
  input  in_3,
  input  in_4,
  input  in_5,
  input  in_6,
  input  in_7,
  input  in_8,
  input  in_9,
  input  in_10,
  input  in_11,
  output out_12,
  output out_13,
  output out_14,
  output out_15,
  output out_16
);

  wire ula_1_out_7, ula_2_out_7, ula_3_out_7;

  ULA ula_1 (.a0(in_2), .b0(in_3), .in_1(in_1), .out_7(ula_1_out_7), .in_4(in_10), .in_5(in_11), .out_6(out_12));
  ULA ula_2 (.a0(in_4), .b0(in_5), .in_1(ula_1_out_7), .out_7(ula_2_out_7), .in_4(in_10), .in_5(in_11), .out_6(out_13));
  ULA ula_3 (.a0(in_6), .b0(in_7), .in_1(ula_2_out_7), .out_7(ula_3_out_7), .in_4(in_10), .in_5(in_11), .out_6(out_14));
  ULA ula_4 (.a0(in_8), .b0(in_9), .in_1(ula_3_out_7), .out_7(out_16), .in_4(in_10), .in_5(in_11), .out_6(out_15));
endmodule

module Multiplexador (
  input  x,
  input  y,
  input  z,
  input  k,
  input  in_5,
  input  in_6,
  output out_7
);

  wire and_1_out, and_2_out, and_3_out, and_4_out, and_5_out, and_6_out, and_7_out, and_8_out, not_1_out,
       not_2_out, not_3_out, not_4_out, or_1_out, or_2_out;

  not not_1 (not_1_out, in_6);
  not not_2 (not_2_out, in_5);
  not not_3 (not_3_out, in_5);
  not not_4 (not_4_out, in_6);
  and and_1 (and_1_out, x, not_1_out);
  and and_2 (and_2_out, y, not_3_out);
  and and_3 (and_3_out, z, in_5);
  and and_4 (and_4_out, k, in_5);
  and and_5 (and_5_out, and_1_out, not_2_out);
  and and_6 (and_6_out, and_2_out, in_6);
  and and_7 (and_7_out, and_3_out, not_4_out);
  and and_8 (and_8_out, and_4_out, in_6);
  or or_1 (or_1_out, and_5_out, and_6_out);
  or or_2 (or_2_out, and_7_out, and_8_out);
  or or_3 (out_7, or_1_out, or_2_out);
endmodule

module ULA (
  input  in_1,
  input  a0,
  input  b0,
  input  in_4,
  input  in_5,
  output out_6,
  output out_7
);

  wire and_1_out, not_1_out, or_1_out, somador_1_out_4;

  and and_1 (and_1_out, a0, b0);
  or or_1 (or_1_out, a0, b0);
  not not_1 (not_1_out, a0);
  Somador somador_1 (.in_2(a0), .in_3(b0), .in_1(in_1), .out_4(somador_1_out_4), .out_5(out_7));
  Multiplexador multiplexador_1 (
    .x(and_1_out), .y(or_1_out), .z(not_1_out), .k(somador_1_out_4), .in_5(in_4), .in_6(in_5), .out_7(out_6));

  // Notes on the sheet:
  //   s
  //   x
  //   y
  //   z
  //   k
endmodule

module Somador (
  input  in_1,
  input  in_2,
  input  in_3,
  output out_4,
  output out_5
);

  wire and_1_out, and_2_out, xor_1_out;

  xor xor_1 (xor_1_out, in_2, in_3);
  and and_1 (and_1_out, in_2, in_3);
  xor xor_2 (out_4, xor_1_out, in_1);
  and and_2 (and_2_out, xor_1_out, in_1);
  or or_1 (out_5, and_2_out, and_1_out);
endmodule
