// Logisim project Decodificador.circ as structural Verilog
module main (
  input  in_1,
  input  in_2,
  input  in_3,
  input  in_4,
  input  in_5,
  input  in_6,
  input  in_7,
  input  in_8,
  output out_9
);

  wire dec_1_a_2, dec_1_b_2, dec_1_c_2, dec_1_d_2, dec_1_e, dec_1_f, dec_1_g, dec_2_a_2, dec_2_b_2,
       dec_2_c_2, dec_2_d_2, dec_2_e, dec_2_f, dec_2_g, dec_3_a_2, dec_3_b_2, dec_3_c_2, dec_3_d_2, dec_3_e,
       dec_3_f, dec_3_g, teste_1_out_11, teste_1_out_12, teste_1_out_13, teste_1_out_14;

  dec dec_1 (
    .A(in_1), .B(in_2), .C(in_3), .D(in_4), .a_2(dec_1_a_2), .b_2(dec_1_b_2), .c_2(dec_1_c_2),
    .d_2(dec_1_d_2), .e(dec_1_e), .f(dec_1_f), .g(dec_1_g));
  dec dec_2 (
    .A(in_5), .B(in_6), .C(in_7), .D(in_8), .a_2(dec_2_a_2), .b_2(dec_2_b_2), .c_2(dec_2_c_2),
    .d_2(dec_2_d_2), .e(dec_2_e), .f(dec_2_f), .g(dec_2_g));
  _7_Segment_Display u_7_segment_display_1 (
    .g(dec_1_g), .f(dec_1_f), .a(dec_1_a_2), .b(dec_1_b_2), .e(dec_1_e), .d(dec_1_d_2), .c(dec_1_c_2));  // open: dp
  _7_Segment_Display u_7_segment_display_2 (
    .g(dec_2_g), .f(dec_2_f), .a(dec_2_a_2), .b(dec_2_b_2), .e(dec_2_e), .d(dec_2_d_2), .c(dec_2_c_2));  // open: dp
  Teste teste_1 (
    .b4(in_5), .a4(in_1), .b3(in_6), .a3(in_2), .b2(in_7), .a1(in_3), .b1(in_8), .a1_2(in_4), .in_9(1'b0),
    .out_10(out_9), .out_11(teste_1_out_11), .out_12(teste_1_out_12), .out_13(teste_1_out_13),
    .out_14(teste_1_out_14));
  dec dec_3 (
    .A(teste_1_out_11), .B(teste_1_out_12), .C(teste_1_out_13), .D(teste_1_out_14), .a_2(dec_3_a_2),
    .b_2(dec_3_b_2), .c_2(dec_3_c_2), .d_2(dec_3_d_2), .e(dec_3_e), .f(dec_3_f), .g(dec_3_g));
  _7_Segment_Display u_7_segment_display_3 (
    .g(dec_3_g), .f(dec_3_f), .a(dec_3_a_2), .b(dec_3_b_2), .e(dec_3_e), .d(dec_3_d_2), .c(dec_3_c_2));  // open: dp
endmodule

module decodificador (
  input  A,
  input  B,
  input  C,
  input  D,
  output a_2,
  output b_2,
  output c_2,
  output d_2,
  output e,
  output f,
  output g
);

  wire and_1_out, and_2_out, and_3_out, and_4_out, and_5_out, and_6_out, and_7_out, and_8_out, and_9_out,
       and_10_out, and_11_out, and_12_out, and_13_out, and_14_out, and_15_out, and_16_out, and_17_out,
       and_18_out, and_19_out, and_20_out, and_21_out, and_22_out, and_23_out, and_24_out, and_25_out,
       and_26_out, and_27_out, and_28_out, and_29_out, and_30_out, and_31_out, not_1_out, not_2_out,
       not_3_out, not_4_out, not_5_out, not_6_out, not_7_out, not_8_out, not_9_out, not_10_out, not_11_out,
       not_12_out, not_13_out, not_14_out, not_15_out, not_16_out, not_17_out, not_18_out, not_19_out,
       not_20_out, not_21_out, not_22_out, not_23_out, not_24_out, not_25_out, not_26_out, not_27_out,
       not_28_out, not_29_out, not_30_out, not_31_out, not_32_out, not_33_out, not_34_out, not_35_out,
       not_36_out, not_37_out, not_38_out, not_39_out;

  not not_1 (not_1_out, A);
  and and_1 (and_1_out, not_1_out, not_2_out);
  not not_2 (not_2_out, C);
  not not_3 (not_3_out, B);
  and and_2 (and_2_out, not_3_out, not_4_out);
  not not_4 (not_4_out, C);
  not not_5 (not_5_out, B);
  and and_3 (and_3_out, not_5_out, not_6_out);
  not not_6 (not_6_out, D);
  not not_7 (not_7_out, C);
  and and_4 (and_4_out, not_7_out, not_8_out);
  not not_8 (not_8_out, D);
  not not_9 (not_9_out, A);
  and and_5 (and_5_out, not_9_out, B, D);
  and and_6 (and_6_out, A, C);
  not not_10 (not_10_out, A);
  and and_7 (and_7_out, not_10_out, not_11_out);
  not not_11 (not_11_out, C);
  not not_12 (not_12_out, A);
  and and_8 (and_8_out, not_12_out, not_13_out);
  not not_13 (not_13_out, D);
  not not_14 (not_14_out, B);
  and and_9 (and_9_out, not_14_out, D);
  not not_15 (not_15_out, B);
  and and_10 (and_10_out, not_15_out, C);
  not not_16 (not_16_out, C);
  and and_11 (and_11_out, B, not_16_out, not_17_out);
  not not_17 (not_17_out, D);
  not not_18 (not_18_out, B);
  not not_19 (not_19_out, A);
  and and_12 (and_12_out, not_19_out, D);
  not not_20 (not_20_out, A);
  and and_13 (and_13_out, not_20_out, C);
  and and_14 (and_14_out, A, not_21_out);
  not not_21 (not_21_out, C);
  not not_22 (not_22_out, A);
  and and_15 (and_15_out, not_22_out, not_23_out);
  not not_23 (not_23_out, C);
  not not_24 (not_24_out, B);
  and and_16 (and_16_out, not_24_out, not_25_out);
  not not_25 (not_25_out, D);
  not not_26 (not_26_out, A);
  and and_17 (and_17_out, not_26_out, B, D);
  and and_18 (and_18_out, B, not_27_out, D);
  not not_27 (not_27_out, C);
  not not_28 (not_28_out, B);
  and and_19 (and_19_out, A, not_28_out, C);
  and and_20 (and_20_out, A, C, not_29_out);
  not not_29 (not_29_out, D);
  not not_30 (not_30_out, B);
  and and_21 (and_21_out, not_30_out, not_31_out);
  not not_31 (not_31_out, D);
  not not_32 (not_32_out, C);
  and and_22 (and_22_out, not_32_out, not_33_out);
  not not_33 (not_33_out, D);
  and and_23 (and_23_out, A, B);
  not not_34 (not_34_out, B);
  and and_24 (and_24_out, not_34_out, not_35_out);
  not not_35 (not_35_out, D);
  and and_25 (and_25_out, B, C);
  and and_26 (and_26_out, A, C);
  and and_27 (and_27_out, A, B);
  not not_36 (not_36_out, A);
  and and_28 (and_28_out, not_36_out, B);
  and and_29 (and_29_out, B, not_37_out);
  not not_37 (not_37_out, C);
  and and_30 (and_30_out, A, not_38_out, not_39_out);
  not not_38 (not_38_out, B);
  not not_39 (not_39_out, D);
  and and_31 (and_31_out, A, C, D);
  or or_1 (b_2, and_7_out, and_8_out, and_9_out, and_10_out, and_11_out);
  or or_2 (c_2, not_18_out, and_12_out, and_13_out, and_14_out);
  or or_3 (e, and_21_out, and_22_out, and_23_out);
  or or_4 (f, and_24_out, and_25_out, and_26_out, and_27_out);
  or or_5 (g, and_28_out, and_29_out, and_30_out, and_31_out);
  or or_6 (a_2, and_1_out, and_2_out, and_3_out, and_4_out, and_5_out, and_6_out);
  or or_7 (d_2, and_15_out, and_16_out, and_17_out, and_18_out, and_19_out, and_20_out);
endmodule

module CLA (
  input  b4,
  input  a4,
  input  b3,
  input  a3,
  input  b2,
  input  a1,
  input  b1,
  input  a1_2,
  input  in_9,
  output out_10,
  output out_11,
  output out_12,
  output out_13,
  output out_14
);

  wire nand_1_out, nand_2_out, nand_3_out, nand_4_out, nand_5_out, nand_6_out, nand_7_out, nand_8_out,
       nand_9_out, nand_10_out, nand_11_out, nand_12_out, nand_13_out, nand_14_out, nand_15_out, nand_16_out,
       nand_17_out, nand_18_out, nand_19_out, nand_20_out, nand_21_out, nand_22_out, nand_23_out,
       nand_24_out, nand_25_out, nand_26_out, nand_27_out, nand_28_out, nand_29_out, nand_30_out,
       nand_31_out, nand_32_out, nand_33_out, nand_34_out, nor_1_out, nor_2_out, nor_3_out, nor_4_out,
       not_1_out, not_2_out, not_3_out, not_4_out, not_5_out, not_6_out, not_7_out, not_8_out, not_9_out,
       not_10_out, not_11_out, not_12_out, not_13_out, not_14_out, not_15_out, not_16_out, not_17_out,
       not_18_out, not_19_out, not_20_out, not_21_out, not_22_out, not_23_out, not_24_out, not_25_out,
       not_26_out, not_27_out, not_28_out, not_29_out, not_30_out, not_31_out, not_32_out, not_33_out,
       not_34_out, not_35_out;

  not not_1 (not_1_out, b4);
  not not_2 (not_2_out, a4);
  not not_3 (not_3_out, b3);
  not not_4 (not_4_out, a3);
  not not_5 (not_5_out, b2);
  not not_6 (not_6_out, a1);
  not not_7 (not_7_out, b1);
  not not_8 (not_8_out, a1_2);
  not not_9 (not_9_out, in_9);
  nor nor_1 (nor_1_out, not_1_out, not_2_out);
  nand nand_1 (nand_1_out, not_1_out, not_2_out);
  nor nor_2 (nor_2_out, not_3_out, not_4_out);
  nand nand_2 (nand_2_out, not_3_out, not_4_out);
  nor nor_3 (nor_3_out, not_5_out, not_6_out);
  nand nand_3 (nand_3_out, not_5_out, not_6_out);
  nor nor_4 (nor_4_out, not_7_out, not_8_out);
  nand nand_4 (nand_4_out, not_7_out, not_8_out);
  not not_10 (not_10_out, nor_1_out);
  not not_11 (not_11_out, nand_1_out);
  not not_12 (not_12_out, nor_2_out);
  not not_13 (not_13_out, nand_2_out);
  not not_14 (not_14_out, nor_3_out);
  not not_15 (not_15_out, nand_3_out);
  not not_16 (not_16_out, nor_4_out);
  not not_17 (not_17_out, nand_4_out);
  not not_18 (not_18_out, not_11_out);
  not not_19 (not_19_out, not_13_out);
  not not_20 (not_20_out, not_15_out);
  not not_21 (not_21_out, not_17_out);
  not not_22 (not_22_out, not_11_out);
  nand nand_5 (nand_5_out, not_13_out, not_10_out);
  nand nand_6 (nand_6_out, not_15_out, not_10_out, not_12_out);
  nand nand_7 (nand_7_out, not_17_out, not_10_out, not_12_out, not_14_out);
  nand nand_8 (nand_8_out, not_10_out, not_12_out, not_14_out, not_16_out, not_9_out);
  nand nand_9 (nand_9_out, not_10_out, not_18_out);
  not not_23 (not_23_out, not_13_out);
  nand nand_10 (nand_10_out, not_17_out, not_12_out, not_14_out);
  nand nand_11 (nand_11_out, not_12_out, not_14_out, not_16_out, not_9_out);
  nand nand_12 (nand_12_out, not_12_out, not_19_out);
  not not_24 (not_24_out, not_15_out);
  not not_25 (not_25_out, not_17_out);
  nand nand_13 (nand_13_out, not_15_out, not_12_out);
  nand nand_14 (nand_14_out, not_17_out, not_14_out);
  nand nand_15 (nand_15_out, not_14_out, not_16_out, not_9_out);
  nand nand_16 (nand_16_out, not_14_out, not_20_out);
  nand nand_17 (nand_17_out, not_16_out, not_9_out);
  nand nand_18 (nand_18_out, not_16_out, not_21_out);
  nand nand_19 (nand_19_out, not_22_out, nand_5_out, nand_6_out, nand_7_out, nand_8_out);
  nand nand_20 (nand_20_out, not_23_out, nand_13_out, nand_10_out, nand_11_out);
  nand nand_21 (nand_21_out, not_24_out, nand_14_out, nand_15_out);
  nand nand_22 (nand_22_out, not_25_out, nand_17_out);
  not not_26 (not_26_out, nand_19_out);
  not not_27 (not_27_out, nand_9_out);
  not not_28 (not_28_out, nand_20_out);
  not not_29 (not_29_out, nand_12_out);
  not not_30 (not_30_out, nand_21_out);
  not not_31 (not_31_out, nand_16_out);
  not not_32 (not_32_out, nand_22_out);
  not not_33 (not_33_out, nand_18_out);
  not not_34 (not_34_out, not_9_out);
  not not_35 (not_35_out, not_26_out);
  nand nand_23 (nand_23_out, not_27_out, not_28_out);
  nand nand_24 (nand_24_out, nand_9_out, nand_20_out);
  nand nand_25 (nand_25_out, not_29_out, not_30_out);
  nand nand_26 (nand_26_out, nand_12_out, nand_21_out);
  nand nand_27 (nand_27_out, not_31_out, not_32_out);
  nand nand_28 (nand_28_out, nand_16_out, nand_22_out);
  nand nand_29 (nand_29_out, not_33_out, not_34_out);
  nand nand_30 (nand_30_out, nand_18_out, not_9_out);
  not not_36 (out_10, not_35_out);
  nand nand_31 (nand_31_out, nand_23_out, nand_24_out);
  nand nand_32 (nand_32_out, nand_29_out, nand_30_out);
  not not_37 (out_11, nand_31_out);
  not not_38 (out_12, nand_33_out);
  nand nand_33 (nand_33_out, nand_25_out, nand_26_out);
  nand nand_34 (nand_34_out, nand_27_out, nand_28_out);
  not not_39 (out_13, nand_34_out);
  not not_40 (out_14, nand_32_out);
endmodule

module dec (
  input  A,
  input  B,
  input  C,
  input  D,
  output a_2,
  output b_2,
  output c_2,
  output d_2,
  output e,
  output f,
  output g
);

  wire and_1_out, and_2_out, and_3_out, and_4_out, and_5_out, and_6_out, and_7_out, and_8_out, and_9_out,
       and_10_out, and_11_out, and_12_out, and_13_out, and_14_out, and_15_out, and_16_out, and_17_out,
       and_18_out, and_19_out, and_20_out, and_21_out, and_22_out, and_23_out, and_24_out, and_25_out,
       and_26_out, and_27_out, and_28_out, and_29_out, and_30_out, and_31_out, and_32_out, and_33_out,
       and_34_out, and_35_out, not_1_out, not_2_out, not_3_out, not_4_out, not_5_out, not_6_out, not_7_out,
       not_8_out, not_9_out, not_10_out, not_11_out, not_12_out, not_13_out, not_14_out, not_15_out,
       not_16_out, not_17_out, not_18_out, not_19_out, not_20_out, not_21_out, not_22_out, not_23_out,
       not_24_out, not_25_out, not_26_out, not_27_out, not_28_out, not_29_out, not_30_out, not_31_out,
       not_32_out, not_33_out, not_34_out, not_35_out, not_36_out, not_37_out, not_38_out, not_39_out,
       not_40_out, not_41_out, not_42_out, not_43_out, not_44_out;

  not not_1 (not_1_out, B);
  and and_1 (and_1_out, not_1_out, not_2_out);
  not not_2 (not_2_out, D);
  not not_3 (not_3_out, A);
  and and_2 (and_2_out, not_3_out, C);
  not not_4 (not_4_out, A);
  and and_3 (and_3_out, not_4_out, B, D);
  and and_4 (and_4_out, B, C);
  not not_5 (not_5_out, B);
  and and_5 (and_5_out, A, not_5_out, not_6_out);
  not not_6 (not_6_out, C);
  and and_6 (and_6_out, A, not_7_out);
  not not_7 (not_7_out, D);
  not not_8 (not_8_out, A);
  and and_7 (and_7_out, not_8_out, not_9_out);
  not not_9 (not_9_out, B);
  not not_10 (not_10_out, A);
  and and_8 (and_8_out, not_10_out, not_11_out, not_12_out);
  not not_11 (not_11_out, C);
  not not_12 (not_12_out, D);
  not not_13 (not_13_out, B);
  and and_9 (and_9_out, not_13_out, not_14_out);
  not not_14 (not_14_out, D);
  not not_15 (not_15_out, A);
  and and_10 (and_10_out, not_15_out, C, D);
  and and_11 (and_11_out, A, not_16_out, D);
  not not_16 (not_16_out, C);
  not not_17 (not_17_out, A);
  and and_12 (and_12_out, not_17_out, not_18_out);
  not not_18 (not_18_out, C);
  not not_19 (not_19_out, A);
  and and_13 (and_13_out, not_19_out, D);
  not not_20 (not_20_out, C);
  and and_14 (and_14_out, not_20_out, D);
  not not_21 (not_21_out, A);
  and and_15 (and_15_out, not_21_out, B);
  and and_16 (and_16_out, A, not_22_out);
  not not_22 (not_22_out, B);
  not not_23 (not_23_out, A);
  not not_24 (not_24_out, B);
  and and_17 (and_17_out, not_23_out, not_24_out, not_25_out);
  not not_25 (not_25_out, D);
  not not_26 (not_26_out, B);
  and and_18 (and_18_out, not_26_out, C, D);
  not not_27 (not_27_out, C);
  and and_19 (and_19_out, B, not_27_out, D);
  and and_20 (and_20_out, B, C, not_28_out);
  not not_28 (not_28_out, D);
  and and_21 (and_21_out, A, not_29_out, not_30_out);
  not not_29 (not_29_out, C);
  not not_30 (not_30_out, D);
  not not_31 (not_31_out, B);
  and and_22 (and_22_out, not_31_out, not_32_out);
  not not_32 (not_32_out, D);
  and and_23 (and_23_out, C, not_33_out);
  not not_33 (not_33_out, D);
  and and_24 (and_24_out, A, C);
  and and_25 (and_25_out, A, B);
  not not_34 (not_34_out, C);
  and and_26 (and_26_out, not_34_out, not_35_out);
  not not_35 (not_35_out, D);
  not not_36 (not_36_out, A);
  and and_27 (and_27_out, not_36_out, B, not_37_out);
  not not_37 (not_37_out, C);
  and and_28 (and_28_out, B, not_38_out);
  not not_38 (not_38_out, D);
  and and_29 (and_29_out, A, not_39_out);
  not not_39 (not_39_out, B);
  and and_30 (and_30_out, A, C);
  not not_40 (not_40_out, B);
  and and_31 (and_31_out, not_40_out, C);
  and and_32 (and_32_out, C, not_41_out);
  not not_41 (not_41_out, D);
  not not_42 (not_42_out, A);
  and and_33 (and_33_out, not_42_out, B, not_43_out);
  not not_43 (not_43_out, C);
  and and_34 (and_34_out, A, not_44_out);
  not not_44 (not_44_out, B);
  and and_35 (and_35_out, A, D);
  or or_1 (b_2, and_7_out, and_8_out, and_9_out, and_10_out, and_11_out);
  or or_2 (c_2, and_12_out, and_13_out, and_14_out, and_15_out, and_16_out);
  or or_3 (d_2, and_17_out, and_18_out, and_19_out, and_20_out, and_21_out);
  or or_4 (e, and_22_out, and_23_out, and_24_out, and_25_out);
  or or_5 (f, and_26_out, and_27_out, and_28_out, and_29_out, and_30_out);
  or or_6 (g, and_31_out, and_32_out, and_33_out, and_34_out, and_35_out);
  or or_7 (a_2, and_1_out, and_2_out, and_3_out, and_4_out, and_5_out, and_6_out);
endmodule

module Teste (
  input  b4,
  input  a4,
  input  b3,
  input  a3,
  input  b2,
  input  a1,
  input  b1,
  input  a1_2,
  input  in_9,
  output out_10,
  output out_11,
  output out_12,
  output out_13,
  output out_14
);

  wire nand_1_out, nand_2_out, nand_3_out, nand_4_out, nand_5_out, nand_6_out, nand_7_out, nand_8_out,
       nand_9_out, nand_10_out, nand_11_out, nand_12_out, nand_13_out, nand_14_out, nand_15_out, nand_16_out,
       nand_17_out, nand_18_out, nand_19_out, nand_20_out, nand_21_out, nand_22_out, nand_23_out,
       nand_24_out, nand_25_out, nand_26_out, nand_27_out, nand_28_out, nand_29_out, nand_30_out,
       nand_31_out, nand_32_out, nand_33_out, nand_34_out, nor_1_out, nor_2_out, nor_3_out, nor_4_out,
       not_1_out, not_2_out, not_3_out, not_4_out, not_5_out, not_6_out, not_7_out, not_8_out, not_9_out,
       not_10_out, not_11_out, not_12_out, not_13_out, not_14_out, not_15_out, not_16_out, not_17_out,
       not_18_out, not_19_out, not_20_out, not_21_out, not_22_out, not_23_out, not_24_out, not_25_out,
       not_26_out, not_27_out, not_28_out, not_29_out, not_30_out, not_31_out, not_32_out, not_33_out,
       not_34_out, not_35_out;

  not not_1 (not_1_out, b4);
  not not_2 (not_2_out, a4);
  not not_3 (not_3_out, b3);
  not not_4 (not_4_out, a3);
  not not_5 (not_5_out, b2);
  not not_6 (not_6_out, a1);
  not not_7 (not_7_out, b1);
  not not_8 (not_8_out, a1_2);
  not not_9 (not_9_out, in_9);
  nor nor_1 (nor_1_out, not_1_out, not_2_out);
  nand nand_1 (nand_1_out, not_1_out, not_2_out);
  nor nor_2 (nor_2_out, not_3_out, not_4_out);
  nand nand_2 (nand_2_out, not_3_out, not_4_out);
  nor nor_3 (nor_3_out, not_5_out, not_6_out);
  nand nand_3 (nand_3_out, not_5_out, not_6_out);
  nor nor_4 (nor_4_out, not_7_out, not_8_out);
  nand nand_4 (nand_4_out, not_7_out, not_8_out);
  not not_10 (not_10_out, nor_1_out);
  not not_11 (not_11_out, nand_1_out);
  not not_12 (not_12_out, nor_2_out);
  not not_13 (not_13_out, nand_2_out);
  not not_14 (not_14_out, nor_3_out);
  not not_15 (not_15_out, nand_3_out);
  not not_16 (not_16_out, nor_4_out);
  not not_17 (not_17_out, nand_4_out);
  not not_18 (not_18_out, not_11_out);
  not not_19 (not_19_out, not_13_out);
  not not_20 (not_20_out, not_15_out);
  not not_21 (not_21_out, not_17_out);
  not not_22 (not_22_out, not_11_out);
  nand nand_5 (nand_5_out, not_13_out, not_10_out);
  nand nand_6 (nand_6_out, not_15_out, not_10_out, not_12_out);
  nand nand_7 (nand_7_out, not_17_out, not_10_out, not_12_out, not_14_out);
  nand nand_8 (nand_8_out, not_10_out, not_12_out, not_14_out, not_16_out, not_9_out);
  nand nand_9 (nand_9_out, not_10_out, not_18_out);
  not not_23 (not_23_out, not_13_out);
  nand nand_10 (nand_10_out, not_17_out, not_12_out, not_14_out);
  nand nand_11 (nand_11_out, not_12_out, not_14_out, not_16_out, not_9_out);
  nand nand_12 (nand_12_out, not_12_out, not_19_out);
  not not_24 (not_24_out, not_15_out);
  not not_25 (not_25_out, not_17_out);
  nand nand_13 (nand_13_out, not_15_out, not_12_out);
  nand nand_14 (nand_14_out, not_17_out, not_14_out);
  nand nand_15 (nand_15_out, not_14_out, not_16_out, not_9_out);
  nand nand_16 (nand_16_out, not_14_out, not_20_out);
  nand nand_17 (nand_17_out, not_16_out, not_9_out);
  nand nand_18 (nand_18_out, not_16_out, not_21_out);
  nand nand_19 (nand_19_out, not_22_out, nand_5_out, nand_6_out, nand_7_out, nand_8_out);
  nand nand_20 (nand_20_out, not_23_out, nand_13_out, nand_10_out, nand_11_out);
  nand nand_21 (nand_21_out, not_24_out, nand_14_out, nand_15_out);
  nand nand_22 (nand_22_out, not_25_out, nand_17_out);
  not not_26 (not_26_out, nand_19_out);
  not not_27 (not_27_out, nand_9_out);
  not not_28 (not_28_out, nand_20_out);
  not not_29 (not_29_out, nand_12_out);
  not not_30 (not_30_out, nand_21_out);
  not not_31 (not_31_out, nand_16_out);
  not not_32 (not_32_out, nand_22_out);
  not not_33 (not_33_out, nand_18_out);
  not not_34 (not_34_out, not_9_out);
  not not_35 (not_35_out, not_26_out);
  nand nand_23 (nand_23_out, not_27_out, not_28_out);
  nand nand_24 (nand_24_out, nand_9_out, nand_20_out);
  nand nand_25 (nand_25_out, not_29_out, not_30_out);
  nand nand_26 (nand_26_out, nand_12_out, nand_21_out);
  nand nand_27 (nand_27_out, not_31_out, not_32_out);
  nand nand_28 (nand_28_out, nand_16_out, nand_22_out);
  nand nand_29 (nand_29_out, not_33_out, not_34_out);
  nand nand_30 (nand_30_out, nand_18_out, not_9_out);
  not not_36 (out_10, not_35_out);
  nand nand_31 (nand_31_out, nand_23_out, nand_24_out);
  nand nand_32 (nand_32_out, nand_29_out, nand_30_out);
  not not_37 (out_11, nand_31_out);
  not not_38 (out_12, nand_33_out);
  nand nand_33 (nand_33_out, nand_25_out, nand_26_out);
  nand nand_34 (nand_34_out, nand_27_out, nand_28_out);
  not not_39 (out_13, nand_34_out);
  not not_40 (out_14, nand_32_out);
endmodule
